# Fritzing sketch SoE (saved by Fritzing 0.9.4)

parts:
  U1 = ESP8266 NodeMCU LoLin module
  RS232_to_TTL_Converter = mystery part, 6 pins [chip_label="RS232 to TTL"]
  Debug_Terminal_(optional) = mystery part, 3 pins [chip_label="Debug Terminal"]

nets:
  N1: U1.D1, Debug_Terminal_(optional).pin2
  N2: U1.D2, Debug_Terminal_(optional).pin3
  N3: U1.3V3, RS232_to_TTL_Converter.pin4
  N4: U1.D7, RS232_to_TTL_Converter.pin5
  N5: U1.D8, RS232_to_TTL_Converter.pin6
  N6: U1.RX, RS232_to_TTL_Converter.pin3
  N7: U1.TX, RS232_to_TTL_Converter.pin2
  N8: U1.GND, RS232_to_TTL_Converter.pin1, Debug_Terminal_(optional).pin1

custom parts:
  ESP8266 NodeMCU LoLin module: ESP8266 based NodeMCU
